// Logisim project kalkulu.circ as structural Verilog: 4 circuits, main circuit main
module main (
  input  CMD,
  input  in_2,
  input  in_3,
  input  in_4,
  input  IN1,
  input  in_6,
  input  in_7,
  input  in_8,
  input  IN2,
  input  in_10,
  input  in_11,
  input  in_12
);

  wire and_1_out, and_2_out, and_3_out, clock_1_out, not_1_out, not_2_out, not_3_out,
       quad_pulse_triggered_d_flip_flop_1_q1, quad_pulse_triggered_d_flip_flop_1_q2,
       quad_pulse_triggered_d_flip_flop_1_q3, quad_pulse_triggered_d_flip_flop_1_q4, s_r_ff_1_qn;

  Clock #(.highDuration(1), .lowDuration(1)) clock_1 (.out(clock_1_out));
  and and_1 (and_1_out, clock_1_out, s_r_ff_1_qn);
  quad_pulse_triggered_D_flip_flop quad_pulse_triggered_d_flip_flop_1 (
    .D1(CMD), .D2(in_2), .D3(in_3), .D4(in_4), .Clock(and_1_out), .Q1(quad_pulse_triggered_d_flip_flop_1_q1),
    .Q2(quad_pulse_triggered_d_flip_flop_1_q2), .Q3(quad_pulse_triggered_d_flip_flop_1_q3),
    .Q4(quad_pulse_triggered_d_flip_flop_1_q4));
  quad_pulse_triggered_D_flip_flop quad_pulse_triggered_d_flip_flop_2 (
    .D1(IN1), .D2(in_6), .D3(in_7), .D4(in_8), .Clock(and_1_out));  // open: Q1, Q2, Q3, Q4
  quad_pulse_triggered_D_flip_flop quad_pulse_triggered_d_flip_flop_3 (
    .D1(IN2), .D2(in_10), .D3(in_11), .D4(in_12), .Clock(and_1_out));  // open: Q1, Q2, Q3, Q4
  not not_1 (not_1_out, quad_pulse_triggered_d_flip_flop_1_q1);
  and and_2 (and_2_out, not_1_out, not_2_out);
  not not_2 (not_2_out, quad_pulse_triggered_d_flip_flop_1_q2);
  and and_3 (and_3_out, and_2_out, not_3_out, quad_pulse_triggered_d_flip_flop_1_q4);
  not not_3 (not_3_out, quad_pulse_triggered_d_flip_flop_1_q3);
  // AND_Gate and_4 has open pins: in0=and_2_out, in1=quad_pulse_triggered_d_flip_flop_1_q3, out=open
  S_R_Flip_Flop #(.trigger("rising")) s_r_ff_1 (.Qn(s_r_ff_1_qn), .preset(and_3_out));  // open: S, clk, R, Q, reset, en

  // Notes on the sheet:
  //   00XX
  //   HLT (0001)
  //   001X
endmodule

module gated_D_latch (
  input  D,
  input  E,
  output Q,
  output Q_not
);

  wire nand_1_out, nand_2_out;

  nand nand_1 (nand_1_out, D, E);
  nand nand_2 (nand_2_out, nand_1_out, E);
  nand nand_3 (Q, nand_1_out, Q_not);
  nand nand_4 (Q_not, Q, nand_2_out);
endmodule

module pulse_triggered_D_flip_flop (
  input  D,
  input  Clock,
  output Q,
  output Q_not
);

  wire gated_d_latch_1_q, not_1_out;

  gated_D_latch gated_d_latch_1 (.D(D), .E(Clock), .Q(gated_d_latch_1_q));  // open: Q_not
  not not_1 (not_1_out, Clock);
  gated_D_latch gated_d_latch_2 (.D(gated_d_latch_1_q), .E(not_1_out), .Q(Q), .Q_not(Q_not));
endmodule

module quad_pulse_triggered_D_flip_flop (
  input  Clock,
  input  D1,
  input  D2,
  input  D3,
  input  D4,
  output Q1,
  output Q2,
  output Q3,
  output Q4
);

  pulse_triggered_D_flip_flop pulse_triggered_d_flip_flop_1 (.D(D1), .Clock(Clock), .Q(Q1));  // open: Q_not
  pulse_triggered_D_flip_flop pulse_triggered_d_flip_flop_2 (.D(D2), .Clock(Clock), .Q(Q2));  // open: Q_not
  pulse_triggered_D_flip_flop pulse_triggered_d_flip_flop_3 (.D(D3), .Clock(Clock), .Q(Q3));  // open: Q_not
  pulse_triggered_D_flip_flop pulse_triggered_d_flip_flop_4 (.D(D4), .Clock(Clock), .Q(Q4));  // open: Q_not
endmodule
